# Fritzing sketch KegFillStation (saved by Fritzing 1.0.4)
breadboards: 1

parts:
  WeMos_D1_Mini1 = WeMos D1 Mini
  Part1 = LCD1602-I2C
  Part2 = HX711 Weighing Sensor Module
  RE1 = KY-040 Rotary encoder [package=THT]
  Load_Cell1 = Load Cell - Red/white/black/green

nets:
  3.3V: WeMos_D1_Mini1.3V3, Part2.VCC, RE1.Vcc
  5V: WeMos_D1_Mini1.5V, Part1.VCC
  N1: WeMos_D1_Mini1.D1, Part1.SCL
  N2: WeMos_D1_Mini1.D2, Part1.SDA
  N3: WeMos_D1_Mini1.D3, RE1.SW
  N4: WeMos_D1_Mini1.D4, RE1.DT
  N5: WeMos_D1_Mini1.D5, Part2.DO/RX
  N6: WeMos_D1_Mini1.D6, Part2.CK/TX
  N7: WeMos_D1_Mini1.D7, RE1.CLK
  GND: WeMos_D1_Mini1.G, Part1.GND, Part2.GND, RE1.GND
  N8: Part2.E+, Load_Cell1.wire1
  N9: Part2.E-, Load_Cell1.wire3
  N10: Part2.A+, Load_Cell1.wire2
  N11: Part2.A-, Load_Cell1.wire4

custom parts:
  WeMos D1 Mini: The D1 mini is a mini wifi board based on ESP-8266EX.
  LCD1602-I2C: A standard character display, usually with 2x16 characters. Comes in many colors with LCM1602 IIC attached.
  KY-040 Rotary encoder: KY-040 Rotary Encoder with switch on breakout borad from AZ Delivery
  Load Cell - Red/white/black/green: A rectangle load cell/weighting pressure Sensor with four wires - Red, white, black, green. Normally corresponding with E+, E-, A+, A- respectively.
